// Digital circuit CPU.dig as structural Verilog
module CPU (
  input  clk,
  input  reset,
  output [7:0] Mq,
  output [7:0] Ac
);

  wire clk_alu, clk_t, comparator_1_eq, not_1_out, not_2_out, not_3_out, or_1_out, q, stop_16, str;
  wire [2:0] Opcode;
  wire [7:0] driver_1_out, driver_3_out, out_PC, valor_d;

  EEPROMDualPort #(.AddrBits(3), .Bits(3)) u_Opcode (
    .A(out_PC[2:0]), .Din(3'b000), .str(1'b0), .C(clk_t), .ld(1'b1), .D(Opcode));
  EEPROMDualPort #(.AddrBits(8), .Bits(8)) valor (
    .A(out_PC), .Din(driver_1_out), .str(str), .C(clk_t), .ld(1'b1), .D(valor_d));
  Counter #(.Bits(8)) counter_1 (.en(q), .C(clk_t), .clr(reset), .out(out_PC));  // open: ovf
  not not_1 (not_1_out, str);
  assign driver_1_out = not_1_out ? valor_d : 8'bz;  // Driver driver_1
  assign driver_1_out = str ? Ac : 8'bz;  // Driver driver_2
  not not_2 (not_2_out, str);
  assign driver_3_out = not_2_out ? driver_1_out : 8'bz;  // Driver driver_3
  // ALU alu_1: pin names not known; wires that end beside it: driver_3_out, Opcode, clk_alu, {8{1'b0}}, Ac, Mq
  T_FF t_ff_1 (.T(1'b1), .C(clk_t), .nQ(q));  // open: Q
  and and_1 (clk_t, ~stop_16, clk);  // And
  Comparator #(.Bits(8)) stop (.a(8'h7), .b(out_PC), .eq(stop_16));  // open: gt, lt
  or or_1 (or_1_out, stop_16, str);
  Comparator #(.Bits(3)) comparator_1 (.a(3'b110), .b(Opcode), .eq(comparator_1_eq));  // open: gt, lt
  not not_3 (not_3_out, or_1_out);
  and and_2 (str, comparator_1_eq, q);
  and and_3 (clk_alu, clk_t, not_3_out, q);

  // Notes on the sheet:
  //   contents of Opcode (hex, n*v repeats v):
  //   6*0,6,7
  //   contents of valor (hex, n*v repeats v):
  //   0,1,2,3,4,5,0,0,8,b,c,d,e,e,f,10
endmodule
